# Fritzing sketch 1.ServoBasic (saved by Fritzing 0.9.3b)
breadboards: 1

parts:
  Part1 = Arduino Nano (Rev3.0)
  J1 = Basic Servo
  USBTTL1 = USB TTL Serial Cable

nets:
  GND: Part1.GND, J1.gnd, USBTTL1.GND
  N1: Part1.D11/MOSI, J1.pulse
  VCC: J1.vcc, USBTTL1.5V

notes:
  External USB power plug
  (Not to Raspberry Pi)
