# Fritzing sketch 1.Servo (saved by Fritzing 0.9.3b)
breadboards: 1

parts:
  Part1 = Arduino Nano (Rev3.0)
  C1 = Ceramic Capacitor [package="100 mil [THT, multilayer]"]  # not connected
  C2 = Ceramic Capacitor [package="100 mil [THT, multilayer]"]  # not connected
  J1 = Basic Servo

nets:
  GND: Part1.GND, J1.gnd
  N1: Part1.D11/MOSI, J1.pulse
  5V: Part1.5V, J1.vcc

custom parts:
  Ceramic Capacitor: 100 nF multilayer Ceramic Capacitor
