# Fritzing sketch 3.Accel (saved by Fritzing 0.9.3b)
breadboards: 1

parts:
  Part1 = Arduino Nano (Rev3.0)
  C1 = Ceramic Capacitor [package="100 mil [THT, multilayer]"]  # not connected
  C2 = Ceramic Capacitor [package="100 mil [THT, multilayer]"]  # not connected
  OLED_I2C1 = OLED 128x64 I2C Monochrome Display
  IC1 = DIP - 10 pins [chip_label=ADXL345 package="DIP (Dual Inline) [THT]"]

nets:
  GND: Part1.GND, OLED_I2C1.GND, IC1.GND
  5V: Part1.5V, OLED_I2C1.VDD, IC1.5V
  N1: Part1.A5, OLED_I2C1.SCK, IC1.SCL
  N2: Part1.A4, OLED_I2C1.SDA, IC1.SDA

custom parts:
  Ceramic Capacitor: 100 nF multilayer Ceramic Capacitor
  DIP - 10 pins: A DIP stand-in part for whatever IC you want. With 10 pins on a 900mil dual inline package (DIP) footprint.
