# Fritzing sketch 3.UltrasoundBasic (saved by Fritzing 0.9.3b)
breadboards: 1

parts:
  hc-sr1 = hc-sr04
  Part1 = Arduino Nano (Rev3.0)

nets:
  VCC: hc-sr1.VCC, Part1.5V
  N1: hc-sr1.Trig, Part1.D2
  N2: hc-sr1.Echo, Part1.D3
  GND: hc-sr1.GND, Part1.GND
