# Fritzing sketch 5.Encoders (saved by Fritzing 0.9.3b)
breadboards: 1

parts:
  Part1 = Arduino Nano (Rev3.0)
  LED1 = RGB LED (com. cathode, rgb) [package="5 mm [THT]"]
  LED2 = RGB LED (com. cathode, rgb) [package="5 mm [THT]"]
  LED3 = RGB LED (com. cathode, rgb) [package="5 mm [THT]"]
  LED4 = RGB LED (com. cathode, rgb) [package="5 mm [THT]"]
  ENCODER1 = Rotary Encoder with Knob bth

nets:
  GND: Part1.GND, LED1.common_cathode, LED2.common_cathode, LED3.common_cathode, LED4.common_cathode, ENCODER1.VIN
  N1: Part1.D2, LED4.blue_anode
  N2: Part1.D3, ENCODER1.B
  N3: Part1.D4, ENCODER1.S
  N4: Part1.D5, ENCODER1.GND
  N5: Part1.5V, LED1.green_anode, LED2.green_anode, LED3.green_anode, LED4.green_anode, ENCODER1.A
  N6: LED1.red_anode, LED2.blue_anode
  N7: LED1.blue_anode, LED4.red_anode
  N8: LED2.red_anode, LED3.blue_anode

custom parts:
  Rotary Encoder with Knob bth: Rotary Encoder with 1/4" Shaft and Knob
