# Fritzing sketch 5.Infrared (saved by Fritzing 0.9.3b)
breadboards: 1

parts:
  Part1 = Arduino Nano (Rev3.0)
  LED2 = smd LED [color="White (4500K)" package="1206 [SMD]"]
  LED3 = smd LED [color="Infrared (940nm)" package="1206 [SMD]"]
  R2 = Resistor [package="2010 [SMD]"]
  R3 = Resistor [tolerance=±5% resistance=220 package=THT]

nets:
  N1: Part1.GND, LED2.anode, LED3.cathode
  N2: Part1.D3, LED2.cathode, R3.Pin_1
  N3: Part1.5V, R2.Pin_0, R3.Pin_0
  N4: LED3.anode, R2.Pin_1

custom parts:
  Resistor: Resistor Basic schematic elements and footprints for 0603, 1206, and PTH resistors.
