# Fritzing sketch 5.Infrared_windmill (saved by Fritzing 0.9.3b)
breadboards: 1

parts:
  Part1 = Arduino Nano (Rev3.0)
  JP1 = Header 1 [package=1x01_offset]
  JP2 = Header 1 [package=1x01_offset]
  JP3 = Header 1 [package=1x01_offset]
  JP4 = Header 1 [package=1x01_offset]

nets:
  N1: Part1.GND, JP4.1
  N2: Part1.D3, JP2.1
  N3: Part1.D4, JP1.1
  N4: Part1.5V, JP3.1
