# Fritzing sketch 6.WiFi (saved by Fritzing 0.9.3b)
breadboards: 1

parts:
  Part1 = Arduino Nano (Rev3.0)
  LED1 = RGB LED - (4 legs) [package="5 mm [THT]"]
  Part3 = Logic Level Converter
  U1 = ESP8266 WiFi Module [part_number=ESP8266]  # not connected
  IC1 = IC, DIP package, 8 pins [chip_label=IC]
  USBTTL1 = USB TTL Serial Cable
  C1 = Capacitor Polarized [package=cpol-radial-10uf-25v]
  R1 = Resistor [tolerance=±5% resistance=10k package=THT]
  R2 = Resistor [tolerance=±5% resistance=10k package=THT]
  LED2 = RGB LED - (4 legs) [package="5 mm [THT]"]

nets:
  GND: Part1.GND, LED1.common_anode, Part3.GND, USBTTL1.GND, C1.-, LED2.common_anode
  N1: Part1.D2, Part3.TX_HV
  N2: Part1.D3, Part3.RX_HV
  N3: Part1.D5, LED1.blue_cathode
  N4: Part1.5V, LED1.green_cathode, Part3.HV, LED2.green_cathode
  N5: LED1.red_cathode, Part3.TX2_HV, LED2.blue_cathode
  N6: Part3.LV, IC1.pin8, USBTTL1.5V, C1.+, R1.Pin_1, R2.Pin_1
  N7: Part3.TX_LV, IC1.pin5
  N8: IC1.pin6, R2.Pin_0
  N9: IC1.pin7, R1.Pin_0

notes:
  External Power - 3.3V
  to USB charger
  <- Check orientation
  <- Reset wire

custom parts:
  ESP8266 WiFi Module: Generic WiFi Module based on the ESP8266 with onboard PCB antenna and UART communications
