# Fritzing sketch 7.Bluetooth[Conflict] (saved by Fritzing 0.9.3b)
breadboards: 1

parts:
  Part1 = Arduino Nano (Rev3.0)
  Part2 = Bluetooth HC-06
  LED1 = RGB LED - (4 legs) [package="5 mm [THT]"]
  Part3 = Logic Level Converter

nets:
  N1: Part1.D1/TX, Part3.TX_HV
  N2: Part1.D0/RX, Part3.RX_HV
  GND: Part1.GND, Part2.GND, LED1.common_anode, Part3.GND
  N3: Part1.D6, LED1.blue_cathode
  5V: Part1.5V, Part2.VCC, LED1.green_cathode, Part3.HV
  N4: Part1.3V3, Part3.LV
  N5: Part2.RXD, Part3.RX_LV
  N6: Part2.TXD, Part3.TX_LV
  N7: LED1.red_cathode, Part3.TX2_HV
