# Fritzing sketch 8.ColorSensor (saved by Fritzing 0.9.3b)
breadboards: 1

parts:
  Part1 = Arduino Nano (Rev3.0)
  C1 = Ceramic Capacitor [package="100 mil [THT, multilayer]"]  # not connected
  C2 = Ceramic Capacitor [package="100 mil [THT, multilayer]"]  # not connected
  Part2 = Adafruit TCS34725 RGB Color Sensor [part_number="Adafruit #1334"]
  LED1 = RGB LED - (4 legs) [package="5 mm [THT]"]

nets:
  GND: Part1.GND, Part2.GND, LED1.common_anode
  N1: Part1.D2, LED1.blue_cathode
  N2: Part1.D9, Part2.LED_EN
  5V: Part1.5V, Part2.VIN, LED1.green_cathode
  N3: Part1.A5, Part2.SDA
  N4: Part1.A4, Part2.SCL

custom parts:
  Ceramic Capacitor: 100 nF multilayer Ceramic Capacitor
  Adafruit TCS34725 RGB Color Sensor: Your electronics can now see in dazzling color with this lovely color light sensor. We found the best color sensor on the market, the TCS34725, which has RGB and Clear light sensing elements. An IR blocking filter, integrated on-chip and localized to the color sensing photodiodes, minimizes the IR spectral component of the incoming light and allows color measurements to be made accurately. The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
