# Fritzing sketch 9.SoundGraph (saved by Fritzing 0.9.3b)
breadboards: 1

parts:
  Part1 = Arduino Nano (Rev3.0)
  Part2 = Bicolor 8x8 LED Matrix Backpack [part_number=902]
  Part3 = Breakout Board for Electret Microphone

nets:
  GND: Part1.GND, Part2.GND, Part3.GND
  5V: Part1.5V, Part2.VDD, Part3.VCC
  N1: Part1.A6, Part3.AUD
  N2: Part1.A4, Part2.SCL

custom parts:
  Bicolor 8x8 LED Matrix Backpack: This 1.2" bi-color 8x8 LED matrix includes a driver chip for simple control via an I2C interface. It's called a Bicolor LED, but you can have 3 colors total by turning on the red and green LEDs, which creates yellow. That's 3 colors for the price of 2! The backpacks come with address-selection jumpers so you can connect up to eight bicolor matrices on a single I2C bus.
