# Fritzing sketch 1.PuzzleMaze (saved by Fritzing 0.9.3b)
breadboards: 1

parts:
  Part1 = Arduino Nano (Rev3.0)
  C1 = Ceramic Capacitor [package="100 mil [THT, multilayer]"]  # not connected
  C2 = Ceramic Capacitor [package="100 mil [THT, multilayer]"]  # not connected
  J1 = Basic Servo
  J2 = Basic Servo
  USBTTL1 = USB TTL Serial Cable
  Part2 = Thumb Joystick

nets:
  GND: Part1.GND, J1.gnd, J2.gnd, USBTTL1.GND, Part2.GND
  N1: Part1.D2, J2.pulse
  N2: Part1.D3, J1.pulse
  N3: Part1.A6, Part2.VERT
  N4: Part1.A5, Part2.HORZ
  VCC: J1.vcc, J2.vcc, USBTTL1.5V, Part2.VCC

notes:
  Game - X
  Game - Y
  External USB Power
  Joystick Pins not same

custom parts:
  Ceramic Capacitor: 100 nF multilayer Ceramic Capacitor
