# Fritzing sketch 10.LaserTripwireBasic (saved by Fritzing 0.9.3b)
breadboards: 1

parts:
  Part1 = Arduino Nano (Rev3.0)
  R1 = PHOTOCELL [package=photocell-kit]
  R2 = Resistor [tolerance=±5% resistance=220 package=THT]
  Part2 = KY-008 Laser Transmitter Module [package="Breakout board"]

nets:
  N1: Part1.GND, R2.Pin_1, Part2.-
  N2: Part1.D6, Part2.S
  N3: Part1.5V, R1.P$1
  N4: Part1.A6, R1.P$2, R2.Pin_0

custom parts:
  KY-008 Laser Transmitter Module: Laser Transmitter module KY-008 for Arduino, emits a dot shaped red laser beam.
