# Fritzing sketch 3.UltrasoundBasic (saved by Fritzing 0.9.3b)
breadboards: 1

parts:
  Part1 = Arduino Nano (Rev3.0)
  Part2 = SRF05 Ultrasonic Rangefinder

nets:
  GND: Part1.GND, Part2.GND
  N1: Part1.D2, Part2.Trig
  N2: Part1.D3, Part2.Echo
  5V: Part1.5V, Part2.VCC
