# Fritzing sketch 5.Encoders (saved by Fritzing 0.9.3b)
breadboards: 1

parts:
  Part1 = Arduino Nano (Rev3.0)
  ENCODER1 = Rotary Encoder with Knob bth

nets:
  GND: Part1.GND, ENCODER1.VIN
  N1: Part1.D4, ENCODER1.S
  N2: Part1.D5, ENCODER1.GND
  N3: Part1.5V, ENCODER1.A

custom parts:
  Rotary Encoder with Knob bth: Rotary Encoder with 1/4" Shaft and Knob
