# Fritzing sketch 9.AudioBasic (saved by Fritzing 0.9.3b)
breadboards: 1

parts:
  Part1 = Arduino Nano (Rev3.0)
  Part3 = Breakout Board for Electret Microphone

nets:
  GND: Part1.GND, Part3.GND
  N1: Part1.5V, Part3.AUD
  N2: Part1.A6, Part3.VCC
